# Fritzing sketch esb (saved by Fritzing 0.9.2b)
breadboards: 1

parts:
  R1 = Resistor [tolerance=±5% resistance=330 package="0603 [SMD]"]
  LeftLED1 = LED - 5mm [color="Red (633nm)" package="5 mm [THT]"]
  LeftLED2 = LED - 5mm [color="Red (633nm)" package="5 mm [THT]"]
  LeftLED3 = LED - 5mm [color="Red (633nm)" package="5 mm [THT]"]
  RightLED1 = LED - 5mm [color="Green (555nm)" package="5 mm [THT]"]
  RightLED2 = LED - 5mm [color="Green (555nm)" package="5 mm [THT]"]
  RightLED3 = LED - 5mm [color="Green (555nm)" package="5 mm [THT]"]
  Left = Pushbutton [package=THT]
  Right = Pushbutton [package=THT]
  R7 = Resistor [tolerance=±5% resistance=110 package="0603 [SMD]"]
  Q1 = PNP-Transistor [package="TO92 [THT]"]
  Raspberry_Pi_A1 = Raspberry Pi A
  J1 = Piezo Speaker
  Right_Ground = BANANA_CONN [package=banana_conn]
  Left_Ground = BANANA_CONN [package=banana_conn]

nets:
  N1: R1.Pin_0, Left.leg0, Right.leg0, Raspberry_Pi_A1.3V3
  N2: R1.Pin_1, LeftLED1.cathode
  N3: LeftLED1.anode, LeftLED2.anode, LeftLED3.anode, Raspberry_Pi_A1.GPIO_17
  N4: RightLED1.cathode, R7.Pin_1
  N5: RightLED1.anode, RightLED2.anode, RightLED3.anode, Raspberry_Pi_A1.GPIO_18
  N6: Left.leg1, Raspberry_Pi_A1.GPIO_22
  N7: Right.leg1, Raspberry_Pi_A1.GPIO_23, Raspberry_Pi_A1.GPIO_27, Left_Ground.1
  N8: R7.Pin_0, Raspberry_Pi_A1.5V, J1.pin2
  N9: Q1.E, J1.pin1
  N10: Q1.B, Raspberry_Pi_A1.GPIO_4
  N11: Q1.C, Raspberry_Pi_A1.GND, Raspberry_Pi_A1.GPIO_24, Right_Ground.1

notes:
  Resistors set for each diode
  Brown wires attached to epee ground
